# Fritzing sketch miau (saved by Fritzing 1.0.1rc)
breadboards: 2

parts:
  R1 = Resistor [tolerance=±5% resistance=330 package="2010 [SMD]"]
  R2 = Resistor [tolerance=±5% resistance=330 package="2010 [SMD]"]
  R3 = Resistor [tolerance=±5% resistance=330 package="2010 [SMD]"]
  R4 = Resistor [tolerance=±5% resistance=330 package="2010 [SMD]"]
  R5 = Resistor [tolerance=±5% resistance=330 package="2010 [SMD]"]
  R6 = Resistor [tolerance=±5% resistance=330 package="2010 [SMD]"]
  R7 = Resistor [tolerance=±5% resistance=330 package="2010 [SMD]"]
  R8 = Resistor [tolerance=±5% resistance=10k package="2010 [SMD]"]
  R9 = Resistor [tolerance=±5% resistance=10k package="2010 [SMD]"]
  R10 = Resistor [tolerance=±5% resistance=10k package="2010 [SMD]"]
  R11 = Resistor [tolerance=±5% resistance=10k package="2010 [SMD]"]
  R12 = Resistor [tolerance=±5% resistance=10k package="2010 [SMD]"]
  R13 = Resistor [tolerance=±5% resistance=10k package="2010 [SMD]"]
  R14 = Resistor [tolerance=±5% resistance=10k package="2010 [SMD]"]
  Grove1 = Grove OLED 128x96
  LED1 = LEDs [package=led10mm]
  LED2 = LEDs [package=led10mm]
  LED3 = LEDs [package=led10mm]
  LED4 = LEDs [package=led10mm]
  LED5 = LEDs [package=led10mm]
  LED6 = LEDs [package=led10mm]
  LED7 = LEDs [package=led10mm]
  IR2 = TSOP312.., 314.. [package=THT]
  IR3 = TSOP312.., 314.. [package=THT]
  IR4 = TSOP312.., 314.. [package=THT]
  IR5 = TSOP312.., 314.. [package=THT]
  IR6 = TSOP312.., 314.. [package=THT]
  IR7 = TSOP312.., 314.. [package=THT]
  IR8 = TSOP312.., 314.. [package=THT]
  Mod2 = YL-99 Limit switch and LED
  Componente3 = Arduino Mega 2560 (Rev3)

nets:
  N1: R1.Pin_0, LED7.A
  N2: R1.Pin_1, R2.Pin_1, R3.Pin_1, R4.Pin_1, R5.Pin_1, R6.Pin_1, R7.Pin_1, Grove1.VCC
  N3: R2.Pin_0, LED6.A
  N4: R3.Pin_0, LED5.A
  N5: R4.Pin_0, LED4.A
  N6: R5.Pin_0, LED3.A
  N7: R6.Pin_0, LED2.A
  N8: R7.Pin_0, LED1.A
  N9: R8.Pin_0, IR8.Vs, Componente3.A8
  VCC: R8.Pin_1, R9.Pin_1, R10.Pin_1, R11.Pin_1, R12.Pin_1, R13.Pin_1, R14.Pin_1, Mod2.VCC, Componente3.5V
  N10: R9.Pin_0, IR7.Vs, Componente3.A0
  N11: R10.Pin_0, IR6.Vs, Componente3.A1
  N12: R11.Pin_0, IR5.Vs, Componente3.A6
  N13: R12.Pin_0, IR4.Vs, Componente3.A3
  N14: R13.Pin_0, IR3.Vs, Componente3.A4
  N15: R14.Pin_0, IR2.Vs, Componente3.A5
  GND: Grove1.GND, LED1.C, LED2.C, LED3.C, LED4.C, LED5.C, LED6.C, LED7.C, IR2.GND, IR3.GND, IR4.GND, IR5.GND, IR6.GND, IR7.GND, IR8.GND, Componente3.GND
  N16: Grove1.SDA, Componente3.D20/SDA
  N17: Grove1.SCL, Componente3.D21/SCL
  N18: Mod2.OUT, Componente3.D23

custom parts:
  TSOP312.., 314..: The TSOP312.., TSOP314.. series are miniaturized receivers for infrared remote control systems. A PIN diode and a preamplifier are assembled on a lead frame, the epoxy package acts as an IR filter. The demodulated output signal can be directly decoded by a microprocessor. The TSOP312.. is compatible with all common IR remote control data formats. The TSOP314.. is optimized to suppress almost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
  YL-99 Limit switch and LED: YL-99 limit switch with pullup and LED module.
